# Fritzing sketch fritzing_schema-breadboard (saved by Fritzing 0.9.9b)
breadboards: 1

parts:
  Mod1 = Raspberry Pi 4B
  U1 = PCF8574 [package="DIP16 [THT]"]
  LCD1 = LCD screen
  V1 = DC Power [voltage=5V]
  R1 = Rotary Potentiometer (Small) [maximum_resistance=10kΩ package=THT]
  VALVE1 = Plastic Solenoid Valve
  R2 = Resistor [tolerance=±5% resistance=1k package="2010 [SMD]"]
  YF-S201_Flow_Meter1 = YF-S201 Water Flow Meter
  R3 = Resistor [tolerance=±5% resistance=330 package="0402 [SMD]"]
  A02YYUW = IC, SIP package, 4 pins [chip_label=A02YYUW]
  Power_12V = Power plug
  DF-FIT0212 = IC, SIP package, 3 pins [chip_label=DF]
  V2 = DC Power [voltage=3.3V]
  S1 = Momentary Switch [package=ksa_sealed_tac_switch]
  R4 = Resistor [tolerance=±5% resistance=330 package="0402 [SMD]"]
  Q2 = npn-Powertransistor [part_number=TIP120 package="TO220 [THT]"]
  D1 = Diode [package=diode-1n4001]
  Power_5V = Power plug
  Power_3_3V1 = Power plug

nets:
  N1: Mod1.GPIO2, U1.SDA
  N2: Mod1.GPIO3, U1.SCL
  GND: Mod1.GND, U1.A0, U1.A1, U1.A2, U1.GND, LCD1.VSS, LCD1.R/W, LCD1.LED-, V1.V-, R1.leg2, YF-S201_Flow_Meter1.GND, A02YYUW.pin2, Power_12V.GND, DF-FIT0212.pin3, V2.V-, R4.Pin_1, Q2.emitter, Power_5V.GND, Power_3_3V1.GND
  N3: Mod1.GPIO14, A02YYUW.pin3
  N4: Mod1.GPIO15, A02YYUW.pin4
  N5: Mod1.GPIO17, DF-FIT0212.pin1
  N6: Mod1.GPIO18, R3.Pin_0
  N7: Mod1.GPIO25, LCD1.E
  N8: Mod1.GPIO8, LCD1.RS
  N9: Mod1.GPIO20, S1.4
  N10: Mod1.GPIO21, R2.Pin_0
  N11: U1.P0, LCD1.DB0
  N12: U1.P1, LCD1.DB1
  N13: U1.P2, LCD1.DB2
  N14: U1.P3, LCD1.DB3
  N15: U1.P4, LCD1.DB4
  N16: U1.P5, LCD1.DB5
  N17: U1.P6, LCD1.DB6
  N18: U1.P7, LCD1.DB7
  VCC: U1.VCC, YF-S201_Flow_Meter1.VCC, A02YYUW.pin1, DF-FIT0212.pin2, V2.V+, Power_3_3V1.VCC
  VDD: LCD1.VDD, LCD1.LED+, V1.V+, R1.leg1, Power_5V.VCC
  N19: LCD1.V0, R1.wiper
  N20: VALVE1.no_name_yet#1, Power_12V.VCC, D1.C
  N21: VALVE1.no_name_yet#2, Q2.collector, D1.A
  N22: R2.Pin_1, Q2.base
  N23: YF-S201_Flow_Meter1.SIG, R3.Pin_1
  N24: S1.1, R4.Pin_0

custom parts:
  YF-S201 Water Flow Meter: The YF-S201 Flow Meter. The input voltage is 5V to 24V (DC).
